# Fritzing sketch joystick (saved by Fritzing 0.9.3b)
breadboards: 1

parts:
  Left = Pushbutton [package="[THT]"]
  Up = Pushbutton [package="[THT]"]
  Down = Pushbutton [package="[THT]"]
  Right = Pushbutton [package="[THT]"]
  R4 = Resistor [tolerance=±5% resistance=1k package=THT]
  R5 = Resistor [tolerance=±5% resistance=1k package=THT]
  R6 = Resistor [tolerance=±5% resistance=1k package=THT]
  R7 = Resistor [tolerance=±5% resistance=1k package=THT]
  Push = Pushbutton [package="[THT]"]
  R8 = Resistor [tolerance=±5% resistance=1k package=THT]
  Bauteil2 = Adafruit T-Cobbler Plus [part_number="Adafruit #1989 and #2028"]

nets:
  N1: Left.Pin_1, Left.Pin_2, R5.Pin_1, Bauteil2.GPIO6
  N2: Left.Pin_3, Left.Pin_4, Up.Pin_3, Up.Pin_4, Down.Pin_3, Down.Pin_4, Right.Pin_3, Right.Pin_4, Push.Pin_3, Push.Pin_4, Bauteil2.+3.3V
  N3: Up.Pin_1, Up.Pin_2, R4.Pin_1, Bauteil2.GPIO5
  N4: Down.Pin_1, Down.Pin_2, R6.Pin_1, Bauteil2.GPIO13
  N5: Right.Pin_1, Right.Pin_2, R7.Pin_1, Bauteil2.GPIO19
  N6: R4.Pin_0, R5.Pin_0, R6.Pin_0, R7.Pin_0, R8.Pin_0, Bauteil2.GND
  N7: Push.Pin_1, Push.Pin_2, R8.Pin_1, Bauteil2.GPIO26

custom parts:
  Adafruit T-Cobbler Plus: The Raspberry Pi has landed on the Maker World like a 40-GPIO pinned, quad-USB ported, credit card sized bomb of DIY joy. And while you can use most of our great Model B accessories by hooking up our downgrade cable, its probably a good time to upgrade your set up and accessorize using all of the 40 pins. That's why we now carry the Assembled Adafruit Pi T-Cobbler Plus - Breakout + Cable for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
