# Fritzing sketch ledButton (saved by Fritzing 0.9.3b)
breadboards: 1

parts:
  Bauteil1 = Adafruit T-Cobbler Plus [part_number="Adafruit #1989 and #2028"]
  Button = Pushbutton [package="[THT]"]
  part = LED - 3mm [color="Red (633nm)" package="3 mm [THT]"]
  part_2 = Resistor [tolerance=±5% resistance=68 package=THT]
  part_3 = Resistor [tolerance=±5% resistance=10k package=THT]

nets:
  N1: Bauteil1.+3.3V, Button.Pin_3, Button.Pin_4
  N2: Bauteil1.GND, part.anode, part_3.Pin_1
  N3: Bauteil1.GPIO19, part_2.Pin_1
  N4: Bauteil1.GPIO26, Button.Pin_1, Button.Pin_2, part_3.Pin_0
  N5: part.cathode, part_2.Pin_0

custom parts:
  Adafruit T-Cobbler Plus: The Raspberry Pi has landed on the Maker World like a 40-GPIO pinned, quad-USB ported, credit card sized bomb of DIY joy. And while you can use most of our great Model B accessories by hooking up our downgrade cable, its probably a good time to upgrade your set up and accessorize using all of the 40 pins. That's why we now carry the Assembled Adafruit Pi T-Cobbler Plus - Breakout + Cable for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
